# Fritzing sketch hc-sr04-sensor-circuit-diagram (saved by Fritzing 0.9.4)
breadboards: 1

parts:
  WeMos_D1_Mini1 = WeMos D1 Mini
  R2 = Resistor [tolerance=±5% resistance=330 package=THT]
  R3 = Resistor [tolerance=±5% resistance=330 package=THT]
  HC-SR04_Sensor_2 = HC-SR04 Ultrasonic Distance Sensor

nets:
  5V: WeMos_D1_Mini1.5V, HC-SR04_Sensor_2.VCC
  N1: WeMos_D1_Mini1.D1, R2.Pin_0, R3.Pin_0
  N2: WeMos_D1_Mini1.D2, HC-SR04_Sensor_2.TRIG
  N3: WeMos_D1_Mini1.G, R3.Pin_1, HC-SR04_Sensor_2.GND
  N4: R2.Pin_1, HC-SR04_Sensor_2.ECHO

custom parts:
  HC-SR04 Ultrasonic Distance Sensor: The HC-SR04 is an ultrasonic distance sensor. It is capable of providing measurement for ranges of 2cm to 400cm. The module operates at 5V.
